// Digital circuit ALU.dig as structural Verilog
module ALU (
  input  MODE,
  input  CIN,
  input  [11:0] MUX,
  input  [11:0] AC,
  input  [3:0] S,
  output COUT,
  output [11:0] ALU
);

  wire _74181_1_p1, _74181_2_p2;

  // _74181 _74181_1: pin names not known; wires that end beside it: _74181_1_p1, MUX[3], MUX[2], MUX[1], MUX[0], AC[3], AC[2], AC[1], AC[0], S[0], S[1], S[2], S[3], MODE, 1'b1, ALU[3], ALU[2], ALU[1], ALU[0], COUT
  // _74181 _74181_2: pin names not known; wires that end beside it: 1'b0, _74181_2_p2, MUX[7], MUX[6], MUX[5], MUX[4], AC[7], AC[6], AC[5], AC[4], S[0], S[1], S[2], S[3], MODE, 1'b1, ALU[7], ALU[6], ALU[5], ALU[4], _74181_1_p1
  // _74181 _74181_3: pin names not known; wires that end beside it: 1'b0, CIN, MUX[11], MUX[10], MUX[9], MUX[8], AC[11], AC[10], AC[9], AC[8], S[0], S[1], S[2], S[3], MODE, 1'b1, 1'b0, ALU[11], ALU[10], ALU[9], ALU[8], _74181_2_p2

  // Other names for the same wires on the sheet: ALU0_3[3:0] = ALU[3:0]; ALU4_7[3:0] = ALU[7:4];
  //   ALU8_11[3:0] = ALU[11:8]; AC0_3[3:0] = AC[3:0]; AC4_7[3:0] = AC[7:4]; AC8_11[3:0] = AC[11:8];
  //   MUX0_3[3:0] = MUX[3:0]; MUX4_7[3:0] = MUX[7:4]; MUX8_11[3:0] = MUX[11:8]
endmodule
