// Digital circuit Accumulator-TTL.dig as structural Verilog
module Accumulator_TTL (
  input  CLOCK_H,
  input  AC_S0,
  input  AC_S1,
  input  CLA,
  input  LINK,
  input  [11:0] ALU,
  output [11:0] AC
);

  _74194 _74194_1 (
    .pin1(CLA), .pin2(LINK), .pin3(ALU[0]), .pin4(ALU[1]), .pin5(ALU[2]), .pin6(ALU[3]), .pin7(AC[4]),
    .pin8(1'b0), .pin9(AC_S0), .pin10(AC_S1), .pin11(CLOCK_H), .pin12(AC[3]), .pin13(AC[2]), .pin14(AC[1]),
    .pin15(AC[0]), .pin16(1'b1));
  _74194 _74194_2 (
    .pin1(CLA), .pin2(AC[3]), .pin3(ALU[4]), .pin4(ALU[5]), .pin5(ALU[6]), .pin6(ALU[7]), .pin7(AC[8]),
    .pin8(1'b0), .pin9(AC_S0), .pin10(AC_S1), .pin11(CLOCK_H), .pin12(AC[7]), .pin13(AC[6]), .pin14(AC[5]),
    .pin15(AC[4]), .pin16(1'b1));
  _74194 _74194_3 (
    .pin1(CLA), .pin2(AC[7]), .pin3(ALU[8]), .pin4(ALU[9]), .pin5(ALU[10]), .pin6(ALU[11]), .pin7(LINK),
    .pin8(1'b0), .pin9(AC_S0), .pin10(AC_S1), .pin11(CLOCK_H), .pin12(AC[11]), .pin13(AC[10]), .pin14(AC[9]),
    .pin15(AC[8]), .pin16(1'b1));

  // Other names for the same wires on the sheet: AC0_3[3:0] = AC[3:0]; AC4_7[3:0] = AC[7:4]; AC8_11[3:0] = AC[11:8];
  //   ALU0_3[3:0] = ALU[3:0]; ALU4_7[3:0] = ALU[7:4]; ALU8_11[3:0] = ALU[11:8]

  // Notes on the sheet:
  //   CLA: default 1
  //   S0 S1
  //   0   0   Nothing
  //   1   0   SHR
  //   0   1   SHL
  //   1   1   Load
endmodule
