// Digital circuit Accumulator.dig as structural Verilog
module Accumulator (
  input  CLOCK_H,
  input  AC_S0,
  input  AC_S1,
  input  CLA,
  input  LINK,
  input  [11:0] ALU,
  output [11:0] AC
);

  // _74194real _74194real_1: pin names not known; wires that end beside it: CLA, LINK, AC[4], CLOCK_H, AC_S0, AC_S1, ALU[0], ALU[1], ALU[2], ALU[3], 1'b1, 1'b0, AC[2], AC[3], AC[1], AC[0]
  // _74194real _74194real_2: pin names not known; wires that end beside it: CLA, AC[3], AC[8], CLOCK_H, AC_S0, AC_S1, ALU[4], ALU[5], ALU[6], ALU[7], 1'b1, 1'b0, AC[6], AC[7], AC[5], AC[4]
  // _74194real _74194real_3: pin names not known; wires that end beside it: CLA, AC[7], LINK, CLOCK_H, AC_S0, AC_S1, ALU[8], ALU[9], ALU[10], ALU[11], 1'b1, 1'b0, AC[10], AC[11], AC[9], AC[8]

  // Other names for the same wires on the sheet: AC4_7[3:0] = AC[7:4]; AC8_11[3:0] = AC[11:8]; AC0_3[3:0] = AC[3:0];
  //   ALU0_3[3:0] = ALU[3:0]; ALU4_7[3:0] = ALU[7:4]; ALU8_11[3:0] = ALU[11:8]
endmodule
