// Digital circuit Bitrev.dig as structural Verilog
module Bitrev (
  input  [11:0] I,
  output [11:0] O
);

  // Pins of 1 and 12 bits meet at I
  // Pins of 1 and 12 bits meet at {I[0], I[1], I[2], I[3], I[4], I[5], I[6], I[7], I[8], I[9], I[10], I[11]}

  assign O = {I[0], I[1], I[2], I[3], I[4], I[5], I[6], I[7], I[8], I[9], I[10], I[11]};
endmodule
