// Digital circuit Clock-Logic.dig as structural Verilog
module Clock_Logic (
  input  CLOCK,
  input  nAuto_Manual,
  input  CLOCK_Manual,
  output CLOCK_H,
  output CLOCK_L
);

  wire nand_1_out, nand_2_out, nand_3_out, not_1_out;

  not not_1 (not_1_out, nAuto_Manual);
  nand nand_1 (nand_1_out, CLOCK, not_1_out);
  nand nand_2 (nand_2_out, nAuto_Manual, CLOCK_Manual);
  nand nand_3 (nand_3_out, nand_1_out, nand_2_out);
  T_FF t_ff_1 (.T(1'b1), .C(nand_3_out), .Q(CLOCK_H), .nQ(CLOCK_L));

  // Notes on the sheet:
  //   2:1 MUX for clock input.
endmodule
