// Digital circuit IOT-Logic.dig as structural Verilog
module IOT_Logic (
  input  [11:0] IR,
  input  IOT_H,
  input  CP0_H,
  input  CP1_H,
  input  CP2_H,
  output IOP1_L,
  output IOP2_L,
  output IOP4_L,
  output IOP1_H,
  output IOP2_H,
  output IOP4_H
);

  nand nand_1 (IOP1_L, CP0_H, IOT_H, IR[11]);
  nand nand_2 (IOP2_L, CP1_H, IOT_H, IR[10]);
  nand nand_3 (IOP4_L, CP2_H, IOT_H, IR[9]);
  not not_1 (IOP1_H, IOP1_L);
  not not_2 (IOP2_H, IOP2_L);
  not not_3 (IOP4_H, IOP4_L);
endmodule
