// Digital circuit KeyboardModify.dig as structural Verilog
module KeyboardModify (
  input  [15:0] KBDIN,
  input  KBDCLK,
  output [11:0] KBDOUT
);

  wire lt_LF_gt___eq__0x0A_eq;
  wire [7:0] Data_Latch_q;
  wire [7:7] multiplexer_1_out;

  D_FF #(.Bits(8)) Data_Latch (.D(KBDIN[7:0]), .C(KBDCLK), .Q(Data_Latch_q));  // open: nQ
  Comparator #(.Bits(8)) lt_LF_gt___eq__0x0A (.a(Data_Latch_q), .b(8'ha), .eq(lt_LF_gt___eq__0x0A_eq));  // open: gt, lt
  Multiplexer #(.Bits(8)) multiplexer_1 (
    .sel(lt_LF_gt___eq__0x0A_eq), .in_0(Data_Latch_q), .in_1(8'hd),
    .out({multiplexer_1_out[7], KBDOUT[5], KBDOUT[6], KBDOUT[7], KBDOUT[8], KBDOUT[9], KBDOUT[10], KBDOUT[11]}));

  assign KBDOUT[4:0] = 5'b10000;

  // Notes on the sheet:
  //   <CR> = 0x0D
endmodule
