// Digital circuit LD10-Instruction-Decode.dig as structural Verilog
module LD10_Instruction_Decode (
  input  CLOCK_H,
  input  CONTP_L,
  input  SWONMAP,
  input  CP7_H,
  input  CP7_L,
  input  A0,
  input  [11:0] IR,
  output AND,
  output TAD,
  output ISZ,
  output DCA,
  output JMS,
  output JMP,
  output IOT,
  output MIC,
  output OPG1_H,
  output OPG1_L,
  output OPG2_H,
  output OPG2_L
);

  wire jk_ff_as_1_q, not_1_out;
  wire [2:0] multiplexer_1_out;
  wire [3:3] jk_ff_as_2_q;

  JK_FF_AS jk_ff_as_1 (.Set(~CONTP_L), .J(CP7_H), .C(CLOCK_H), .K(~A0), .Clr(~1'b1), .Q(jk_ff_as_1_q));  // open: nQ
  JK_FF_AS jk_ff_as_2 (
    .Set(~SWONMAP), .J(1'b0), .C(CLOCK_H), .K(~CP7_L), .Clr(~1'b1), .Q(jk_ff_as_2_q[3]));  // open: nQ
  Multiplexer multiplexer_1 (.sel(jk_ff_as_1_q), .in_0(1'b1), .in_1(IR[0]), .out(multiplexer_1_out[2]));
  Multiplexer multiplexer_2 (.sel(jk_ff_as_1_q), .in_0(1'b0), .in_1(IR[2]), .out(multiplexer_1_out[0]));
  Multiplexer multiplexer_3 (.sel(jk_ff_as_1_q), .in_0(1'b0), .in_1(IR[1]), .out(multiplexer_1_out[1]));
  Demultiplexer #(.Selector_Bits(4), .Default(1)) demultiplexer_1 (
    .sel({jk_ff_as_2_q[3], multiplexer_1_out}), .in(1'b0), .out_0(AND), .out_1(TAD), .out_2(ISZ),
    .out_3(DCA), .out_4(JMS), .out_5(JMP), .out_6(IOT), .out_7(MIC));  // open: out_8, out_9, out_10, out_11, out_12, out_13, out_14, out_15
  not not_1 (not_1_out, MIC);
  nor nor_1 (OPG1_H, MIC, IR[3]);
  nand nand_1 (OPG2_L, IR[3], not_1_out);
  not not_2 (OPG1_L, OPG1_H);
  not not_3 (OPG2_H, OPG2_L);

  // Notes on the sheet:
  //   SWONMAP: default 1
  //   Force OPCODE to 4 (JMS) during Interrupt.
  //   Disable IR during manual operation.
endmodule
