// Digital circuit LD11-State-Machine.dig as structural Verilog
module LD11_State_Machine (
  input  CLOCK_H,
  input  [11:0] MA,
  input  DCA,
  input  JMP,
  input  JMS,
  input  MIC,
  input  IOT,
  input  [11:0] IR,
  input  CYCOMP_H,
  input  ION_L,
  input  IIE_L,
  input  FETCH,
  input  nFETCH,
  output A0,
  output A3,
  output A4,
  output A6,
  output A7,
  output A9,
  output F0,
  output F1,
  output F2,
  output F3,
  output F5,
  output F7,
  output F8,
  output F10,
  output FETCH1,
  output FETCH2,
  output FETCH4,
  output FETCH8,
  output DCA_plus_JMP_plus_JMS
);

  wire DERXXX, LD, MA_eq_001X, multiplexer_1_out, nand_1_out, nand_2_out, nand_3_out, nand_4_out, not_3_out,
       not_4_out, not_5_out, not_6_out, not_7_out, not_8_out, not_9_out, not_10_out, not_11_out, not_12_out,
       or_1_out, or_2_out;
  wire [3:0] not_1_out;

  not not_1 (not_1_out[3], A7);
  not not_2 (not_1_out[0], A3);
  nor nor_1 (LD, not_1_out[3], not_1_out[0]);
  not not_3 (not_3_out, MA[0]);
  not not_4 (not_4_out, MA[1]);
  not not_5 (not_5_out, MA[2]);
  not not_6 (not_6_out, MA[3]);
  not not_7 (not_7_out, MA[4]);
  not not_8 (not_8_out, MA[5]);
  not not_9 (not_9_out, MA[6]);
  nand nand_1 (nand_1_out, not_3_out, not_4_out, not_5_out, not_6_out, not_7_out, not_8_out, not_9_out, MA[8]);
  CounterPreset #(.Bits(4)) counterpreset_1 (
    .en(not_12_out), .C(CLOCK_H), .dir(1'b0), .in({not_1_out[3], 2'b00, not_1_out[0]}), .ld(~LD),
    .clr(~FETCH), .out({FETCH8, FETCH4, FETCH2, FETCH1}));  // open: ovf
  nor nor_2 (MA_eq_001X, nand_1_out, MA[7]);
  // Probe on {FETCH8, FETCH4, FETCH2, FETCH1}
  Multiplexer #(.Selector_Bits(4)) multiplexer_1 (
    .sel({FETCH8, FETCH4, FETCH2, FETCH1}), .in_0(IIE_L), .in_1(CYCOMP_H), .in_2(1'b1), .in_3(ION_L),
    .in_4(DERXXX), .in_5(CYCOMP_H), .in_6(IR[3]), .in_7(MA_eq_001X), .in_8(CYCOMP_H),
    .in_9(DCA_plus_JMP_plus_JMS), .in_10(CYCOMP_H), .in_11(1'b0), .in_12(1'b0), .in_13(1'b0), .in_14(1'b0),
    .in_15(1'b0), .out(multiplexer_1_out));
  not not_10 (not_10_out, multiplexer_1_out);
  not not_11 (not_11_out, IR[3]);
  nand nand_2 (nand_2_out, DCA, JMP, JMS);
  not not_12 (not_12_out, not_10_out);
  or or_1 (or_1_out, not_12_out, nFETCH);
  or or_2 (or_2_out, nFETCH, not_10_out);
  nand nand_3 (nand_3_out, not_11_out, nand_2_out);
  not not_13 (DCA_plus_JMP_plus_JMS, nand_2_out);
  Demultiplexer #(.Selector_Bits(4), .Default(1)) demultiplexer_1 (
    .sel({FETCH8, FETCH4, FETCH2, FETCH1}), .in(or_1_out), .out_0(A0), .out_3(A3), .out_4(A4), .out_6(A6),
    .out_7(A7), .out_9(A9));  // open: out_1, out_2, out_5, out_8, out_10, out_11, out_12, out_13, out_14, out_15
  Demultiplexer #(.Selector_Bits(4), .Default(1)) demultiplexer_2 (
    .sel({FETCH8, FETCH4, FETCH2, FETCH1}), .in(or_2_out), .out_0(F0), .out_1(F1), .out_2(F2), .out_3(F3),
    .out_5(F5), .out_7(F7), .out_8(F8), .out_10(F10));  // open: out_4, out_6, out_9, out_11, out_12, out_13, out_14, out_15
  nand nand_4 (nand_4_out, MIC, IOT, nand_3_out);
  not not_14 (DERXXX, nand_4_out);

  // Notes on the sheet:
  //   nFETCH: default 1
endmodule
