// Digital circuit LD12-MUX-Signals.dig as structural Verilog
module LD12_MUX_Signals (
  input  F1,
  input  F3,
  input  F5,
  input  F7,
  input  F8,
  input  F10,
  input  CP0_H,
  input  CP2_H,
  input  CP0_L,
  input  CP2_L,
  input  MANSW_nEX_nRUN,
  input  DEP_plus_EX__CP6,
  input  OPG1_CP3,
  input  AND,
  input  TAD,
  input  ISZ,
  input  DCA,
  input  JMP,
  input  JMS,
  input  IOT,
  input  OPG1_H,
  input  OPG2_H,
  output [2:0] B
);

  wire nand_1_out, nand_2_out, nand_3_out, nand_4_out, nand_5_out, nand_6_out, nand_7_out, nand_8_out,
       nand_9_out, nor_1_out, nor_2_out, nor_3_out, nor_4_out, nor_5_out, nor_6_out, not_1_out, not_2_out,
       not_3_out, not_4_out, not_5_out, not_6_out, not_7_out, not_8_out, not_9_out;

  nand nand_1 (nand_1_out, F1, F5, F10);
  nor nor_1 (nor_1_out, MANSW_nEX_nRUN, CP0_L);
  nand nand_2 (nand_2_out, OPG2_H, CP2_H);
  nor nor_2 (nor_2_out, DCA, CP0_L);
  nand nand_3 (nand_3_out, OPG1_H, CP2_H);
  nor nor_3 (nor_3_out, JMP, CP0_L);
  nor nor_4 (nor_4_out, JMS, CP2_L);
  nand nand_4 (nand_4_out, AND, TAD, ISZ);
  nand nand_5 (nand_5_out, nand_4_out, CP0_H);
  not not_1 (not_1_out, nand_1_out);
  not not_2 (not_2_out, nor_1_out);
  not not_3 (not_3_out, nor_2_out);
  not not_4 (not_4_out, nor_3_out);
  not not_5 (not_5_out, nor_4_out);
  nor nor_5 (nor_5_out, IOT, CP2_L);
  nand nand_6 (nand_6_out, not_2_out, nand_2_out);
  nand nand_7 (nand_7_out, not_3_out, nand_3_out, OPG1_CP3);
  nand nand_8 (nand_8_out, not_4_out, not_5_out, DEP_plus_EX__CP6);
  nand nand_9 (nand_9_out, nand_5_out, F7, F8);
  nor nor_6 (nor_6_out, nor_5_out, nand_6_out);
  not not_6 (not_6_out, nand_6_out);
  not not_7 (not_7_out, nand_7_out);
  not not_8 (not_8_out, nand_8_out);
  not not_9 (not_9_out, nand_9_out);
  nand nand_10 (B[2], F3, not_1_out, nor_6_out);
  nand nand_11 (B[1], F3, not_1_out, not_7_out, not_8_out);
  nand nand_12 (B[0], F3, not_6_out, not_7_out, not_9_out);

  // Notes on the sheet:
  //   B2 = (!CP0L * !(MANSW*!EX*!RUN)) + (CP2H * OPG2H) + (!CP2L * !IOT) + !F1 + !F10 + !F3 + !F5
  //   B1 = !((DEP+EX)*CP6) + (!CP0L * !JMP) + (!CP0L * !DCA) + (CP2H * OPG1H) + (!CP2L * !JMS) + !F1 + !F10 + !F3 + !F5 + !(OPG1*CP3)
  //   B0 = ((!AND+!ISZ+!TAD) * CP0H) + (!CP0L * !DCA) + (!CP0L * !(MANSW*!EX*!RUN)) + (CP2H * OPG2H) + (CP2H * OPG1H) + !F3 + !F7 + !F8 + !(OPG1*CP3)
  //   IR=MA
  //   M
  //   SR'
  //   SR
  //   AC
  //   MA
  //   MB
endmodule
