// Digital circuit LD13-ALU-Signals.dig as structural Verilog
module LD13_ALU_Signals (
  input  CP0_L,
  input  CP2_L,
  input  CP3_H,
  input  CP6_H,
  input  AND,
  input  TAD,
  input  IOT,
  input  IOT_H,
  input  ISZ,
  input  JMS,
  input  OPG1_H,
  input  OPG1_L,
  input  OPG2_H,
  input  OPG2_L,
  input  F2,
  input  F7,
  input  DEP_plus_EX,
  output MODE,
  output CIN,
  output DEP_plus_EX__CP6,
  output OPG1_CP3,
  output [3:0] S
);

  wire nand_1_out, nand_2_out, nand_7_out, nor_1_out, nor_2_out, nor_3_out, nor_5_out, nor_6_out, nor_7_out,
       nor_8_out, nor_9_out, not_1_out, not_2_out, not_3_out, not_4_out, not_5_out, not_6_out, not_7_out;

  nor nor_1 (nor_1_out, IOT_H, OPG2_H);
  nor nor_2 (nor_2_out, TAD, CP0_L);
  nor nor_3 (nor_3_out, CP0_L, AND);
  nor nor_4 (S[2], nor_1_out, CP2_L);
  nor nor_5 (nor_5_out, CP2_L, OPG1_L);
  nand nand_1 (nand_1_out, OPG2_L, IOT, ISZ);
  nand nand_2 (nand_2_out, ISZ, JMS);
  nand nand_3 (DEP_plus_EX__CP6, DEP_plus_EX, CP6_H);
  nand nand_4 (OPG1_CP3, OPG1_H, CP3_H);
  not not_1 (not_1_out, nand_1_out);
  not not_2 (not_2_out, nand_2_out);
  nor nor_6 (nor_6_out, not_1_out, CP0_L);
  nor nor_7 (nor_7_out, not_2_out, CP2_L);
  nor nor_8 (nor_8_out, nor_2_out, nor_3_out);
  nor nor_9 (nor_9_out, nor_3_out, S[2]);
  not not_3 (not_3_out, nor_3_out);
  not not_4 (not_4_out, S[2]);
  not not_5 (not_5_out, nor_5_out);
  not not_6 (not_6_out, nor_6_out);
  not not_7 (not_7_out, nor_7_out);
  nand nand_5 (S[3], nor_8_out, nor_9_out);
  nand nand_6 (MODE, not_3_out, not_4_out, not_5_out);
  nand nand_7 (nand_7_out, not_6_out, not_7_out, DEP_plus_EX__CP6, OPG1_CP3, F2, F7);
  not not_8 (S[0], nor_8_out);
  not not_9 (S[1], nor_9_out);
  not not_10 (CIN, nand_7_out);

  // Notes on the sheet:
  //   S0 = (!AND * !CP0L) + (!CP0L * !TAD)
  //   S1 = (!AND * !CP0L) + (!CP2L * OPG2L) + (!CP2L * IOT)
  //   S2 = (!CP2L * OPG2L) + (!CP2L *IOT)
  //   S3 = (!AND * !CP0L) + (!CP0L * !TAD) + (!CP2L * OPG2L) + (!CP2L * IOT)
  //   MODE = (!AND * !CP0L) + (!CP2L * !OPG1L) + (!CP2L * OPG2L) + (!CP2L * IOT)
  //   (DEP+EX)*CP6 = !((DEP+EX)*!RUN) + !CP6H
  //   OPG1*CP3 = !CP3L + !OPG1H
  //   CIN = (!((DEP+EX)*!RUN) * !CP3L * F2 * F7 * IOT * ISZ * JMS * OPG2L) +
  //              (!((DEP+EX)*!RUN) * CP2L * !CP3L * F2 * F7 * IOT * ISZ * OPG2L) + 
  //              (!((DEP+EX)*!RUN) * F2 * F7 * IOT * ISZ * JMS * !OPG1L * OPG2L) +
  //              (!((DEP+EX)*!RUN) * CP2L * F2 * F7 * IOT * ISZ * !OPG1L * OPG2L) + 
  //              (!((DEP+EX)*!RUN) * CP0L * !CP3L * F2 * F7 * ISZ * JMS) +
  //              (!((DEP+EX)*!RUN) * CP0L * F2 * F7 * ISZ * JMS * !OPG1L) +
  //              (!((DEP+EX)*!RUN) * CP0L * CP2L * !CP3L * F2 * F7) +
  //              (!((DEP+EX)*!RUN) * CP0L * CP2L * F2 * F7 * !OPG1L) + 
  //              (CP0L * !CP3L * !CP6H * F2 * F7 * ISZ * JMS) + 
  //              (CP0L * !CP6H * F2 * F7 * ISZ * JMS * !OPG1L) + 
  //              (CP0L * CP2L * !CP3L * !CP6H * F2 * F7) +
  //              (CP0L * CP2L * !CP6H * F2 * F7 * !OPG1L) +
  //              (CP2L * !CP3L * !CP6H * F2 * F7 * IOT * ISZ * OPG2L) +
  //              (CP2L * !CP6H * F2 * F7 * IOT * ISZ * !OPG1L * OPG2L) + 
  //              (!CP3L * !CP6H * F2 * F7 * IOT * ISZ * JMS * OPG2L) + 
  //              (!CP6H * F2 * F7 * IOT * ISZ * JMS * !OPG1L * OPG2L)
endmodule
