// Digital circuit LD14-PC+IR-Logic.dig as structural Verilog
module LD14_PC_IR_Logic (
  input  CLOCK_H,
  input  CLOCK_L,
  input  LINK,
  input  [11:0] AC,
  input  [11:0] MB,
  input  [11:0] IR,
  input  IOS,
  input  ISZ,
  input  JMP,
  input  IOT_H,
  input  LDPC,
  input  LDIR,
  input  F1,
  input  F2,
  input  CP0_H,
  input  CP0_L,
  input  CP2_H,
  input  OPG2_H,
  input  JMS,
  output PC_L,
  output IR_L
);

  wire nand_1_out, nand_2_out, nand_3_out, nand_4_out, nand_5_out, nand_6_out, nand_7_out, nand_8_out,
       nand_9_out, nand_10_out, nand_11_out, nand_12_out, nand_13_out, nand_14_out, nand_15_out, nand_16_out,
       nand_17_out, nand_18_out, nor_1_out, not_1_out, not_2_out, not_3_out, not_4_out, not_5_out, xor_1_out;

  nor nor_1 (nor_1_out, LDIR, CP0_L);
  nand nand_1 (nand_1_out, ~AC[0], ~AC[1], ~AC[2], ~AC[3], ~AC[4], ~AC[5], ~AC[6], ~AC[7], ~AC[8], ~AC[9], ~AC[10], ~AC[11]);  // NAnd
  nand nand_2 (nand_2_out, ~MB[0], ~MB[1], ~MB[2], ~MB[3], ~MB[4], ~MB[5], ~MB[6], ~MB[7], ~MB[8], ~MB[9], ~MB[10], ~MB[11]);  // NAnd
  not not_1 (not_1_out, nor_1_out);
  nand nand_3 (nand_3_out, not_1_out, F1);
  not not_2 (not_2_out, nand_1_out);
  not not_3 (not_3_out, nand_2_out);
  nand nand_4 (nand_4_out, CLOCK_L, IR_L);
  nand nand_5 (nand_5_out, not_4_out, not_3_out);
  not not_4 (not_4_out, ISZ);
  nand nand_6 (nand_6_out, LINK, IR[7]);
  nand nand_7 (nand_7_out, IR[5], AC[0]);
  nand nand_8 (nand_8_out, IR[6], not_2_out);
  D_FF_AS d_ff_as_1 (.Set(~1'b1), .D(nand_3_out), .C(CLOCK_H), .Clr(~nand_4_out), .Q(IR_L));  // open: nQ
  nand nand_9 (nand_9_out, JMS, nand_5_out);
  nand nand_10 (nand_10_out, nand_6_out, nand_7_out, nand_8_out);
  xor xor_1 (xor_1_out, IR[8], nand_10_out);
  nand nand_11 (nand_11_out, CP2_H, nand_9_out);
  nand nand_12 (nand_12_out, OPG2_H, xor_1_out);
  nand nand_13 (nand_13_out, IOT_H, IOS);
  nand nand_14 (nand_14_out, nand_12_out, nand_13_out);
  not not_5 (not_5_out, nand_14_out);
  nand nand_15 (nand_15_out, not_5_out, JMP, LDPC);
  nand nand_16 (nand_16_out, CP0_H, nand_15_out);
  nand nand_17 (nand_17_out, nand_16_out, F2, nand_11_out);
  nand nand_18 (nand_18_out, CLOCK_L, PC_L);
  D_FF_AS d_ff_as_2 (.Set(~1'b1), .D(nand_17_out), .C(CLOCK_H), .Clr(~nand_18_out), .Q(PC_L));  // open: nQ

  // Notes on the sheet:
  //   AC0
  //   AC <> 0
  //   MB <> 0
  //   AC = 0
  //   MB = 0
endmodule
