// Digital circuit LD16-MicroOP-Decode.dig as structural Verilog
module LD16_MicroOP_Decode (
  input  CP0_H,
  input  CP1_H,
  input  CP2_H,
  input  CP5_H,
  input  CP4_L,
  input  CP6_L,
  input  CP7_H,
  input  CLRP_H,
  input  CLRP_L,
  input  DCA,
  input  TAD,
  input  OPG1_H,
  input  OPG2_H,
  input  RDA,
  input  COUT,
  input  [11:0] IR,
  input  OPG1_CP3_IR11,
  output CLA,
  output CLL,
  output CML,
  output RAL,
  output RAR
);

  wire nand_1_out, nand_2_out, nand_3_out, nand_4_out, nand_5_out, nand_6_out, nand_7_out, nand_8_out,
       nand_9_out, nand_10_out, nand_11_out, nand_14_out, nand_15_out, nor_1_out, not_1_out, not_3_out;

  nand nand_1 (nand_1_out, IR[10], CP5_H);
  nand nand_2 (nand_2_out, IR[10], CP7_H);
  nand nand_3 (nand_3_out, OPG1_H, IR[5], CP0_H);
  nand nand_4 (nand_4_out, CP0_H, OPG1_H, IR[4]);
  nand nand_5 (nand_5_out, OPG2_H, IR[4]);
  nand nand_6 (nand_6_out, OPG1_H, IR[7], CP2_H);
  nand nand_7 (nand_7_out, TAD, OPG1_CP3_IR11);
  nand nand_8 (nand_8_out, nand_1_out, CP4_L);
  nand nand_9 (nand_9_out, nand_2_out, CP6_L);
  nand nand_10 (nand_10_out, nand_3_out, CLRP_L);
  nand nand_11 (nand_11_out, DCA, RDA, nand_5_out);
  not not_1 (not_1_out, nand_7_out);
  nand nand_12 (RAR, nand_8_out, IR[8], OPG1_H);
  nand nand_13 (RAL, nand_9_out, IR[9], OPG1_H);
  nand nand_14 (nand_14_out, CP1_H, nand_11_out);
  nor nor_1 (nor_1_out, COUT, not_1_out);
  not not_2 (CLL, nand_10_out);
  nand nand_15 (nand_15_out, nand_4_out, nand_14_out);
  not not_3 (not_3_out, nor_1_out);
  nor nor_2 (CLA, nand_15_out, CLRP_H);
  nand nand_16 (CML, nand_6_out, not_3_out);

  // Notes on the sheet:
  //   CLRP_L: default 1
endmodule
