// Digital circuit LD17-Registers-MA-MB-PC-IR-EA-Logic.dig as structural Verilog
module LD17_Registers_MA_MB_PC_IR_EA_Logic (
  input  A0,
  input  [11:0] ALU,
  input  MA_L,
  input  MB_L,
  input  PC_L,
  input  IR_L,
  output [11:0] MA,
  output [11:0] MB,
  output [11:0] PC,
  output [11:0] IR,
  output [11:0] EA
);

  wire nand_1_out, nand_2_out, nand_3_out, nand_4_out, nand_5_out;

  D_FF_AS #(.Bits(12)) u_MA (.Set(1'b0), .D(ALU), .C(MA_L), .Clr(~A0), .Q(MA));  // open: nQ
  D_FF_AS #(.Bits(12)) u_PC (.Set(1'b0), .D(ALU), .C(PC_L), .Clr(~1'b1), .Q(PC));  // open: nQ
  D_FF_AS #(.Bits(12)) u_IR (.Set(1'b0), .D(ALU), .C(IR_L), .Clr(~1'b1), .Q({EA[11:5], IR[4:0]}));  // open: nQ
  D_FF_AS #(.Bits(12)) u_MB (.Set(1'b0), .D(ALU), .C(MB_L), .Clr(~1'b1), .Q(MB));  // open: nQ
  nand nand_1 (nand_1_out, IR[4], MA[0]);
  nand nand_2 (nand_2_out, IR[4], MA[1]);
  nand nand_3 (nand_3_out, IR[4], MA[2]);
  nand nand_4 (nand_4_out, IR[4], MA[3]);
  nand nand_5 (nand_5_out, IR[4], MA[4]);
  not not_1 (EA[0], nand_1_out);
  not not_2 (EA[1], nand_2_out);
  not not_3 (EA[2], nand_3_out);
  not not_4 (EA[3], nand_4_out);
  not not_5 (EA[4], nand_5_out);

  assign IR[11:5] = EA[11:5];
endmodule
