// Digital circuit LD18-MUX-ALU.dig as structural Verilog
module LD18_MUX_ALU (
  input  [11:0] PC,
  input  [11:0] MB,
  input  [11:0] MA,
  input  [11:0] AC,
  input  [11:0] IORD,
  input  [11:0] SR,
  input  [11:0] M,
  input  [11:0] EA,
  input  [2:0] B,
  input  [3:0] S,
  input  CIN,
  input  MODE,
  output COUT,
  output [11:0] ALU
);

  wire [11:0] multiplexer_1_out;

  Multiplexer #(.Selector_Bits(3), .Bits(12)) multiplexer_1 (
    .sel(B), .in_0(PC), .in_1(MB), .in_2(MA), .in_3(AC), .in_4(IORD),
    .in_5({SR[0], SR[1], SR[2], SR[3], SR[4], SR[5], SR[6], SR[7], SR[8], SR[9], SR[10], SR[11]}), .in_6(M),
    .in_7(EA), .out(multiplexer_1_out));
  ALU alu_1 (.MODE(MODE), .CIN(CIN), .MUX(multiplexer_1_out), .AC(AC), .S(S), .COUT(COUT), .ALU(ALU));

  // Other names for the same wires on the sheet: SR_t[11:0] = {SR[0], SR[1], SR[2], SR[3], SR[4], SR[5], SR[6], SR[7], SR[8], SR[9], SR[10], SR[11]}
endmodule
