// Digital circuit LD19-AC-Link.dig as structural Verilog
module LD19_AC_Link (
  input  CLOCK_H,
  input  CLA,
  input  CLL,
  input  CML,
  input  RAL,
  input  RAR,
  input  AC_L,
  input  [11:0] ALU,
  output LINK,
  output [11:0] AC
);

  wire AC_S0, AC_S1, LINK_F_F_nq, nand_3_out, nand_4_out, nand_5_out, nand_6_out, nor_1_out, nor_2_out,
       nor_3_out, not_1_out, not_2_out, not_3_out, not_4_out, xor_1_out;

  xor xor_1 (xor_1_out, AC_S0, AC_S1);
  nor nor_1 (nor_1_out, xor_1_out, CML);
  nand nand_1 (AC_S0, AC_L, RAR);
  nand nand_2 (AC_S1, AC_L, RAL);
  not not_1 (not_1_out, AC_S0);
  not not_2 (not_2_out, AC_S1);
  nor nor_2 (nor_2_out, nor_1_out, not_4_out);
  nor nor_3 (nor_3_out, nor_1_out, nand_6_out);
  nand nand_3 (nand_3_out, LINK_F_F_nq, CML);
  nand nand_4 (nand_4_out, not_2_out, AC_S0, AC[11]);
  nand nand_5 (nand_5_out, not_1_out, AC_S1, AC[0]);
  not not_3 (not_3_out, nor_3_out);
  nand nand_6 (nand_6_out, nand_3_out, nand_4_out, nand_5_out);
  not not_4 (not_4_out, nand_6_out);
  Accumulator_TTL accumulator_ttl_1 (
    .CLOCK_H(CLOCK_H), .AC_S0(AC_S0), .AC_S1(AC_S1), .CLA(CLA), .LINK(LINK), .ALU(ALU), .AC(AC));
  JK_FF_AS LINK_F_F (.Set(~1'b1), .J(nor_2_out), .C(CLOCK_H), .K(~not_3_out), .Clr(~CLL), .Q(LINK), .nQ(LINK_F_F_nq));

  // Notes on the sheet:
  //   CLA: default 1
  //   CLL: default 1
endmodule
