// Digital circuit LD20-Memory.dig as structural Verilog
module LD20_Memory (
  input  CLOCK_H,
  input  [11:0] MA,
  input  [11:0] MB,
  input  CLRP_L,
  input  WRITE,
  input  [2:0] Field,
  output [11:0] M,
  output CYCOMP_H,
  output CYCOMP_L
);

  PullDown #(.Bits(3)) pulldown_1 (.out(Field));
  D_FF_AS d_ff_as_1 (.Set(~1'b1), .D(WRITE), .C(CLOCK_H), .Clr(~CLRP_L), .Q(CYCOMP_L), .nQ(CYCOMP_H));
  RAMAsync #(.AddrBits(15), .isProgramMemory("true"), .Bits(12)) RAM (
    .A({Field[0], Field[1], Field[2], MA[0], MA[1], MA[2], MA[3], MA[4], MA[5], MA[6], MA[7], MA[8], MA[9], MA[10], MA[11]}),
    .D({MB[0], MB[1], MB[2], MB[3], MB[4], MB[5], MB[6], MB[7], MB[8], MB[9], MB[10], MB[11]}),
    .we(~CYCOMP_H), .Q({M[0], M[1], M[2], M[3], M[4], M[5], M[6], M[7], M[8], M[9], M[10], M[11]}));

  // Other names for the same wires on the sheet: nRAMWE = CYCOMP_H

  // Notes on the sheet:
  //   CLRP_L: default 1
endmodule
