// Digital circuit LD21-Interrupt-Flag-Logic.dig as structural Verilog
module LD21_Interrupt_Flag_Logic (
  input  CLOCK_H,
  input  [11:0] IR,
  input  IOT,
  input  CP0_L,
  input  A0,
  input  A3,
  input  PINT,
  input  CLRP_L,
  input  nINT_inhibit,
  output ION_L,
  output IOF_L,
  output IOT_H,
  output IIE_L,
  output IE
);

  wire and_1_out, and_2_out, d_ff_as_1_nq, d_ff_as_1_q, nand_1_out, nand_2_out, nor_1_out, nor_2_out,
       nor_3_out, nor_4_out, nor_5_out, not_1_out, not_3_out, not_4_out, not_5_out;

  nor nor_1 (nor_1_out, IR[3], IR[4]);
  nor nor_2 (nor_2_out, IR[5], IR[6]);
  nor nor_3 (nor_3_out, IR[7], IR[8]);
  nor nor_4 (nor_4_out, IOF_L, CP0_L);
  nand nand_1 (nand_1_out, nor_1_out, nor_2_out, nor_3_out);
  not not_1 (not_1_out, nor_4_out);
  nand nand_2 (nand_2_out, not_1_out, A0, A3);
  not not_2 (IOT_H, IOT);
  not not_3 (not_3_out, nand_1_out);
  not not_4 (not_4_out, IR[11]);
  nand nand_3 (ION_L, IOT_H, not_3_out, IR[11]);
  nand nand_4 (IOF_L, IOT_H, not_3_out, not_4_out);
  and and_1 (and_1_out, d_ff_as_1_nq, not_5_out);
  not not_5 (not_5_out, nand_2_out);
  and and_2 (and_2_out, nand_2_out, A3);
  nor nor_5 (nor_5_out, and_1_out, and_2_out);
  D_FF_AS d_ff_as_1 (.Set(~1'b1), .D(nor_5_out), .C(CLOCK_H), .Clr(~CLRP_L), .Q(d_ff_as_1_q), .nQ(d_ff_as_1_nq));
  PullUp pullup_1 (.out(nINT_inhibit));
  and and_3 (IE, d_ff_as_1_q, nINT_inhibit);
  nand nand_5 (IIE_L, IE, PINT);

  // Notes on the sheet:
  //   Force high if not used.
endmodule
