// Digital circuit LD8-Manual-Control-Logic.dig as structural Verilog
module LD8_Manual_Control_Logic (
  input  CLOCK_H,
  input  CLR,
  input  CONT,
  input  RUN,
  input  LDPC,
  input  LDIR,
  input  LDMB,
  input  LDM,
  input  LDMA,
  input  LDAC,
  input  EX,
  input  DEP,
  input  nRUN,
  output CLRP_L,
  output CLRP_H,
  output CONTP_L,
  output DEP_plus_EX,
  output DEP_plus_EX__nRUN,
  output MANSW_nEX_nRUN,
  output SWONMANP,
  output MANSW,
  output CONTP_H
);

  wire d_ff_as_1_q, d_ff_as_2_nq, d_ff_as_3_nq, d_ff_as_4_nq, nand_1_out, nand_4_out, nand_5_out, nand_7_out,
       nor_1_out, not_1_out, not_3_out;

  nand nand_1 (nand_1_out, CLR, CONT);
  nand nand_2 (MANSW, LDMA, LDM, LDMB, LDPC, LDIR, LDAC, EX, DEP);
  nand nand_3 (DEP_plus_EX, DEP, EX);
  D_FF_AS d_ff_as_1 (.Set(~1'b1), .D(nand_1_out), .C(CLOCK_H), .Clr(~1'b1), .Q(d_ff_as_1_q));  // open: nQ
  nand nand_4 (nand_4_out, MANSW, nRUN);
  nand nand_5 (nand_5_out, nRUN, DEP_plus_EX);
  D_FF_AS d_ff_as_2 (.Set(~1'b1), .D(d_ff_as_1_q), .C(CLOCK_H), .Clr(~1'b1), .nQ(d_ff_as_2_nq));  // open: Q
  not not_1 (not_1_out, nand_4_out);
  D_FF_AS d_ff_as_3 (.Set(~1'b1), .D(nand_4_out), .C(CLOCK_H), .Clr(~1'b1), .nQ(d_ff_as_3_nq));  // open: Q
  nand nand_6 (MANSW_nEX_nRUN, not_1_out, EX);
  nand nand_7 (nand_7_out, d_ff_as_1_q, d_ff_as_2_nq);
  not not_2 (DEP_plus_EX__nRUN, nand_5_out);
  nor nor_1 (nor_1_out, nand_7_out, RUN);
  D_FF_AS d_ff_as_4 (.Set(~1'b1), .D(d_ff_as_3_nq), .C(CLOCK_H), .Clr(~1'b1), .nQ(d_ff_as_4_nq));  // open: Q
  not not_3 (not_3_out, nor_1_out);
  nand nand_8 (SWONMANP, d_ff_as_3_nq, d_ff_as_4_nq);
  nor nor_2 (CLRP_H, CLR, not_3_out);
  nor nor_3 (CONTP_H, not_3_out, CONT);
  not not_4 (CLRP_L, CLRP_H);
  not not_5 (CONTP_L, CONTP_H);

  // Notes on the sheet:
  //   CLR: default 1
  //   CONT: default 1
  //   LDPC: default 1
  //   LDIR: default 1
  //   LDMB: default 1
  //   LDM: default 1
  //   LDMA: default 1
  //   LDAC: default 1
  //   EX: default 1
  //   DEP: default 1
  //   Switches
endmodule
