// Digital circuit LD9-FETCH-RUN-EXEC-Logic.dig as structural Verilog
module LD9_FETCH_RUN_EXEC_Logic (
  input  CLOCK_H,
  input  CYCOMP_L,
  input  MIC,
  input  OPG2_H,
  input  CLRP_L,
  input  CONTP_L,
  input  SWONMANP,
  input  STOP,
  input  SING_INST,
  input  [11:0] IR,
  input  A0,
  input  A4,
  input  A6,
  input  A9,
  input  F10,
  output CP0_H,
  output CP1_H,
  output CP2_H,
  output CP3_H,
  output CP5_H,
  output CP6_H,
  output CP7_H,
  output CP0_L,
  output CP2_L,
  output CP3_L,
  output CP4_L,
  output CP6_L,
  output CP7_L,
  output RUN,
  output nRUN,
  output FETCH,
  output nFETCH,
  output EXEC,
  output [3:0] CP_MUX,
  output CP_end,
  output nCP_end
);

  wire CP4_H, demultiplexer_1_out_1, demultiplexer_1_out_5, GTE, GTF, multiplexer_1_out, nand_1_out,
       nand_2_out, nand_3_out, nand_5_out, nand_6_out, nor_1_out, not_1_out, not_2_out;

  nand nand_1 (nand_1_out, CP7_H, RUN);
  nand nand_2 (nand_2_out, MIC, CP3_H);
  nand nand_3 (nand_3_out, OPG2_H, IR[10]);
  nand nand_4 (GTE, A0, A4, A6, A9, F10);
  Multiplexer multiplexer_1 (.sel(OPG2_H), .in_0(CP7_H), .in_1(CP4_H), .out(multiplexer_1_out));
  not not_1 (not_1_out, nand_2_out);
  nor nor_1 (nor_1_out, nand_3_out, CP4_L);
  nand nand_5 (nand_5_out, CYCOMP_L, not_1_out);
  JK_FF_AS EXEC_F_F (.Set(~SWONMANP), .J(GTE), .C(CLOCK_H), .K(~nCP_end), .Clr(~CLRP_L), .Q(EXEC), .nQ(CP_MUX[3]));
  Multiplexer #(.Selector_Bits(3)) multiplexer_2 (
    .sel({IR[0], IR[1], IR[2]}), .in_0(CP2_H), .in_1(CP2_H), .in_2(CP3_H), .in_3(CP3_H), .in_4(CP3_H),
    .in_5(CP2_H), .in_6(CP2_H), .in_7(multiplexer_1_out), .out(CP_end));
  nand nand_6 (nand_6_out, STOP, not_2_out, SING_INST);
  not not_2 (not_2_out, nor_1_out);
  Counter #(.Bits(3)) counter_1 (.en(nand_5_out), .C(CLOCK_H), .clr(~EXEC), .out(CP_MUX[2:0]));  // open: ovf
  nand nand_7 (GTF, CP_end, RUN);
  not not_3 (nCP_end, CP_end);
  Demultiplexer #(.Selector_Bits(4), .Default(1)) demultiplexer_1 (
    .sel(CP_MUX), .in(1'b0), .out_0(CP0_L), .out_1(demultiplexer_1_out_1), .out_2(CP2_L), .out_3(CP3_L),
    .out_4(CP4_L), .out_5(demultiplexer_1_out_5), .out_6(CP6_L), .out_7(CP7_L));  // open: out_8, out_9, out_10, out_11, out_12, out_13, out_14, out_15
  JK_FF_AS RUN_F_F (.Set(~CLRP_L), .J(nand_6_out), .C(CLOCK_H), .K(~1'b1), .Clr(~CONTP_L), .Q(nRUN), .nQ(RUN));
  JK_FF_AS FETCH_F_F (.Set(~CLRP_L), .J(GTE), .C(CLOCK_H), .K(~GTF), .Clr(~CONTP_L), .Q(nFETCH), .nQ(FETCH));
  not not_4 (CP0_H, CP0_L);
  not not_5 (CP1_H, demultiplexer_1_out_1);
  not not_6 (CP2_H, CP2_L);
  not not_7 (CP3_H, CP3_L);
  not not_8 (CP4_H, demultiplexer_1_out_5);
  not not_9 (CP5_H, demultiplexer_1_out_5);
  not not_10 (CP6_H, CP6_L);
  not not_11 (CP7_H, CP7_L);

  // Notes on the sheet:
  //   CLRP_L: default 1
  //   CONTP_L: default 1
  //   SWONMANP: default 1
  //   End Exec always at CP7 and go to Fetch. (Obsolete)
  //   HLT requires CP4
  //   Clear Exec (was CP7).
endmodule
