// Digital circuit PDP-8.dig as structural Verilog
module PDP_8 (
  input  Clock,
  input  CLK_Mode,
  input  Manual_Clock,
  input  [15:0] KBD_IN,
  input  KBD_CLK,
  input  CLR,
  input  LD_PC,
  input  LD_IR,
  input  LD_MB,
  input  LD_MEM,
  input  LD_MA,
  input  LD_AC,
  input  DEPOSIT,
  input  EXAMINE,
  input  CONT,
  input  STOP,
  input  SINGINST,
  input  nCLRIN,
  input  [11:0] SR,
  output [7:0] TTY_OUT,
  output TTY_OUT_PRINT,
  output TTY_enable,
  output TTY_IN_CLK,
  output [7:0] OPCODE,
  output [11:0] PC,
  output [11:0] MB,
  output [11:0] MA,
  output [11:0] AC,
  output [11:0] MEM,
  output [11:0] IR,
  output [31:0] STATE,
  output LINK
);

  wire A0, A3, A4, A6, A7, A9, AC_L, bitrev_3_p2, bitrev_5_p2, CLA, CLL, CLOCK_H, CLOCK_L, CLRP_L, CML,
       CONTP_L, COUT, CP0_H, CP0_L, CP1_H, CP2_H, CP2_L, CP3_H, CP3_L, CP4_L, CP5_H, CP6_H, CP6_L, CP7_H,
       CP7_L, CP_end, CYCOMP_H, CYCOMP_L, DCA_plus_JMP_plus_JMS, DEP_plus_EX, DEP_plus_EX__CP6,
       DEP_plus_EX__nRUN, F0, F1, F2, F3, F5, F7, F8, F10, IIE_L, IOF_L, ION_L, IOP1_H, IOP1_L, IOP2_H,
       IOP2_L, IOP4_H, IOP4_L, IOS, IOS_KEYBOARD, IOS_PRINTER, IOT_H, IR_L, MA_L, MANSW_nEX_nRUN, MB_L,
       nCP_end, nFETCH, nRUN, OPG1_CP3, OPG1_H, OPG1_H_CP3_IR11, OPG1_L, OPG2_H, OPG2_L, PC_L, PINT,
       PINT_KEYBOARD, PINT_PRINTER, RAL, RAR, RDA, RDE, SWONMANP;
  wire [3:3] CP_MUX;
  wire [11:0] AC_t, ALU, EA, INPUT, IR_t, M, MA_t, MB_t, PC_t;

  Clock_Logic clock_logic_1 (
    .CLOCK(Clock), .nAuto_Manual(CLK_Mode), .CLOCK_Manual(Manual_Clock), .CLOCK_H(CLOCK_H), .CLOCK_L(CLOCK_L));
  LD8_Manual_Control_Logic ld8_manual_control_logic_1 (
    .CLOCK_H(CLOCK_H), .CLR(CLR), .CONT(CONT), .RUN(STATE[5]), .LDPC(LD_PC), .LDIR(LD_IR), .LDMB(LD_MB),
    .LDM(LD_MEM), .LDMA(LD_MA), .LDAC(LD_AC), .EX(EXAMINE), .DEP(DEPOSIT), .nRUN(nRUN), .CLRP_L(CLRP_L),
    .CLRP_H(STATE[26]), .CONTP_L(CONTP_L), .DEP_plus_EX(DEP_plus_EX), .DEP_plus_EX__nRUN(DEP_plus_EX__nRUN),
    .MANSW_nEX_nRUN(MANSW_nEX_nRUN), .SWONMANP(SWONMANP), .MANSW(STATE[25]), .CONTP_H(STATE[27]));
  LD21_Interrupt_Flag_Logic ld21_interrupt_flag_logic_1 (
    .CLOCK_H(CLOCK_H), .IR(IR_t), .IOT(OPCODE[6]), .CP0_L(CP0_L), .A0(A0), .A3(A3), .PINT(PINT),
    .CLRP_L(CLRP_L), .ION_L(ION_L), .IOF_L(IOF_L), .IOT_H(IOT_H), .IIE_L(IIE_L), .IE(STATE[3]));
  LD9_FETCH_RUN_EXEC_Logic ld9_fetch_run_exec_logic_1 (
    .CLOCK_H(CLOCK_H), .CYCOMP_L(CYCOMP_L), .MIC(OPCODE[7]), .OPG2_H(OPG2_H), .CLRP_L(CLRP_L),
    .CONTP_L(CONTP_L), .SWONMANP(SWONMANP), .STOP(STOP), .SING_INST(SINGINST), .IR(IR_t), .A0(A0), .A4(A4),
    .A6(A6), .A9(A9), .F10(F10), .CP0_H(CP0_H), .CP1_H(CP1_H), .CP2_H(CP2_H), .CP3_H(CP3_H), .CP5_H(CP5_H),
    .CP6_H(CP6_H), .CP7_H(CP7_H), .CP0_L(CP0_L), .CP2_L(CP2_L), .CP3_L(CP3_L), .CP4_L(CP4_L), .CP6_L(CP6_L),
    .CP7_L(CP7_L), .RUN(STATE[5]), .nRUN(nRUN), .FETCH(STATE[0]), .nFETCH(nFETCH), .EXEC(STATE[1]),
    .CP_MUX({CP_MUX[3], STATE[13], STATE[14], STATE[15]}), .CP_end(CP_end), .nCP_end(nCP_end));
  LD13_ALU_Signals ld13_alu_signals_1 (
    .CP0_L(CP0_L), .CP2_L(CP2_L), .CP3_H(CP3_H), .CP6_H(CP6_H), .AND(OPCODE[0]), .TAD(OPCODE[1]),
    .IOT(OPCODE[6]), .IOT_H(IOT_H), .ISZ(OPCODE[2]), .JMS(OPCODE[4]), .OPG1_H(OPG1_H), .OPG1_L(OPG1_L),
    .OPG2_H(OPG2_H), .OPG2_L(OPG2_L), .F2(F2), .F7(F7), .DEP_plus_EX(DEP_plus_EX), .MODE(STATE[20]),
    .CIN(STATE[24]), .DEP_plus_EX__CP6(DEP_plus_EX__CP6), .OPG1_CP3(OPG1_CP3),
    .S({STATE[16], STATE[17], STATE[18], STATE[19]}));
  // Probe on STATE[20]
  // Probe on {STATE[16], STATE[17], STATE[18], STATE[19]}
  LD11_State_Machine ld11_state_machine_1 (
    .CLOCK_H(CLOCK_H), .MA(MA_t), .DCA(OPCODE[3]), .JMP(OPCODE[5]), .JMS(OPCODE[4]), .MIC(OPCODE[7]),
    .IOT(OPCODE[6]), .IR(IR_t), .CYCOMP_H(CYCOMP_H), .ION_L(ION_L), .IIE_L(IIE_L), .FETCH(STATE[0]),
    .nFETCH(nFETCH), .A0(A0), .A3(A3), .A4(A4), .A6(A6), .A7(A7), .A9(A9), .F0(F0), .F1(F1), .F2(F2),
    .F3(F3), .F5(F5), .F7(F7), .F8(F8), .F10(F10), .FETCH1(STATE[11]), .FETCH2(STATE[10]), .FETCH4(STATE[9]),
    .FETCH8(STATE[8]), .DCA_plus_JMP_plus_JMS(DCA_plus_JMP_plus_JMS));
  LD10_Instruction_Decode ld10_instruction_decode_1 (
    .CLOCK_H(CLOCK_H), .CONTP_L(CONTP_L), .SWONMAP(SWONMANP), .CP7_H(CP_end), .CP7_L(nCP_end), .A0(A0),
    .IR(IR_t), .AND(OPCODE[0]), .TAD(OPCODE[1]), .ISZ(OPCODE[2]), .DCA(OPCODE[3]), .JMS(OPCODE[4]),
    .JMP(OPCODE[5]), .IOT(OPCODE[6]), .MIC(OPCODE[7]), .OPG1_H(OPG1_H), .OPG1_L(OPG1_L), .OPG2_H(OPG2_H),
    .OPG2_L(OPG2_L));
  LD15_MA_MB_AC_Logic ld15_ma_mb_ac_logic_1 (
    .CLOCK_H(CLOCK_H), .CLOCK_L(CLOCK_L), .AND(OPCODE[0]), .TAD(OPCODE[1]), .DCA(OPCODE[3]), .JMS(OPCODE[4]),
    .ISZ(OPCODE[2]), .DEP(DEPOSIT), .LDM(LD_MEM), .LDMA(LD_MA), .LDMB(LD_MB), .LDAC(LD_AC), .CP0_H(CP0_H),
    .CP1_H(CP1_H), .CP2_H(CP2_H), .CP3_H(CP3_H), .CP0_L(CP0_L), .OPG1_H(OPG1_H), .OPG2_H(OPG2_H), .A3(A3),
    .F0(F0), .F3(F3), .F5(F5), .F7(F7), .F8(F8), .F10(F10), .DEP_plus_EX__CP6(DEP_plus_EX__CP6), .RDE(RDE),
    .IR(IR_t), .WRITE(STATE[12]), .AC_L(AC_L), .MA_L(MA_L), .MB_L(MB_L), .OPG1_H_CP3_IR11(OPG1_H_CP3_IR11));
  LD14_PC_IR_Logic ld14_pc_ir_logic_1 (
    .CLOCK_H(CLOCK_H), .CLOCK_L(CLOCK_L), .LINK(LINK), .AC(AC_t), .MB(MB_t), .IR(IR_t), .IOS(IOS),
    .ISZ(OPCODE[2]), .JMP(OPCODE[5]), .IOT_H(IOT_H), .LDPC(LD_PC), .LDIR(LD_IR), .F1(F1), .F2(F2),
    .CP0_H(CP0_H), .CP0_L(CP0_L), .CP2_H(CP2_H), .OPG2_H(OPG2_H), .JMS(OPCODE[4]), .PC_L(PC_L), .IR_L(IR_L));
  LD16_MicroOP_Decode ld16_microop_decode_1 (
    .CP0_H(CP0_H), .CP1_H(CP1_H), .CP2_H(CP2_H), .CP5_H(CP5_H), .CP4_L(CP4_L), .CP6_L(CP6_L), .CP7_H(CP7_H),
    .CLRP_H(STATE[26]), .CLRP_L(CLRP_L), .DCA(OPCODE[3]), .TAD(OPCODE[1]), .OPG1_H(OPG1_H), .OPG2_H(OPG2_H),
    .RDA(RDA), .COUT(COUT), .IR(IR_t), .OPG1_CP3_IR11(OPG1_H_CP3_IR11), .CLA(CLA), .CLL(CLL), .CML(CML),
    .RAL(RAL), .RAR(RAR));
  LD19_AC_Link ld19_ac_link_1 (
    .CLOCK_H(CLOCK_H), .CLA(CLA), .CLL(CLL), .CML(CML), .RAL(RAL), .RAR(RAR), .AC_L(AC_L), .ALU(ALU),
    .LINK(LINK), .AC(AC_t));
  LD20_Memory ld20_memory_1 (
    .CLOCK_H(CLOCK_H), .MA(MA_t), .MB(MB_t), .CLRP_L(CLRP_L), .WRITE(STATE[12]), .M(M), .CYCOMP_H(CYCOMP_H),
    .CYCOMP_L(CYCOMP_L));
  IOT_Logic iot_logic_1 (
    .IR(IR_t), .IOT_H(IOT_H), .CP0_H(CP0_H), .CP1_H(CP1_H), .CP2_H(CP2_H), .IOP1_L(IOP1_L), .IOP2_L(IOP2_L),
    .IOP4_L(IOP4_L), .IOP1_H(IOP1_H), .IOP2_H(IOP2_H), .IOP4_H(IOP4_H));
  // Bitrev bitrev_1: pin names not known; wires that end beside it: AC_t, AC
  // Bitrev bitrev_2: pin names not known; wires that end beside it: M, MEM
  // Bitrev bitrev_3: pin names not known; wires that end beside it: SR, bitrev_3_p2
  LD17_Registers_MA_MB_PC_IR_EA_Logic ld17_registers_ma_mb_pc_ir_ea_logic_1 (
    .A0(A0), .ALU(ALU), .MA_L(MA_L), .MB_L(MB_L), .PC_L(PC_L), .IR_L(IR_L), .MA(MA_t), .MB(MB_t), .PC(PC_t),
    .IR(IR_t), .EA(EA));
  LD12_MUX_Signals ld12_mux_signals_1 (
    .F1(F1), .F3(F3), .F5(F5), .F7(F7), .F8(F8), .F10(F10), .CP0_H(CP0_H), .CP2_H(CP2_H), .CP0_L(CP0_L),
    .CP2_L(CP2_L), .MANSW_nEX_nRUN(MANSW_nEX_nRUN), .DEP_plus_EX__CP6(DEP_plus_EX__CP6), .OPG1_CP3(OPG1_CP3),
    .AND(OPCODE[0]), .TAD(OPCODE[1]), .ISZ(OPCODE[2]), .DCA(OPCODE[3]), .JMP(OPCODE[5]), .JMS(OPCODE[4]),
    .IOT(OPCODE[6]), .OPG1_H(OPG1_H), .OPG2_H(OPG2_H), .B(STATE[23:21]));
  // LD18_MUX_ALU ld18_mux_alu_1: pin names not known; wires that end beside it: PC_t, MB_t, MA_t, AC_t, INPUT, bitrev_3_p2, M, EA, STATE[23:21], {STATE[16], STATE[17], STATE[18], STATE[19]}, STATE[24], STATE[20], COUT, ALU
  TTY_Logic tty_logic_1 (
    .IR(IR_t), .nCLRIN(nCLRIN), .IOP1_H(IOP1_H), .IOP2_H(IOP2_H), .IOP4_H(IOP4_H), .IOP1_L(IOP1_L),
    .TTY_IN_DATA_AVAILABLE(KBD_CLK), .PINT_PRINTER(PINT_PRINTER), .TTY_IN_CLOCK(TTY_IN_CLK),
    .TTY_OUT_PRINT(TTY_OUT_PRINT), .IOS_PRINTER(IOS_PRINTER), .PINT_KEYBOARD(PINT_KEYBOARD),
    .IOS_KEYBOARD(IOS_KEYBOARD), .RDA(RDA), .RDE(RDE));
  KeyboardModify keyboardmodify_1 (.KBDIN(KBD_IN), .KBDCLK(KBD_CLK), .KBDOUT(INPUT));
  // Bitrev bitrev_4: pin names not known; wires that end beside it: IR_t, IR
  // Probe on STATE[23:21]
  // Bitrev bitrev_5: pin names not known; wires that end beside it: ALU, bitrev_5_p2
  // Bitrev bitrev_6: pin names not known; wires that end beside it: PC_t, PC
  // Bitrev bitrev_7: pin names not known; wires that end beside it: MB_t, MB
  // Bitrev bitrev_8: pin names not known; wires that end beside it: MA_t, MA
  // Probe on bitrev_5_p2
  or or_1 (STATE[2], ~F7, ~F8, ~F10);  // Or
  nand nand_1 (PINT, PINT_PRINTER, PINT_KEYBOARD);
  nand nand_2 (IOS, IOS_PRINTER, IOS_KEYBOARD);
  TTYMOD ttymod_1 (
    .TTY_IN({1'b0, AC_t[5], AC_t[6], AC_t[7], AC_t[8], AC_t[9], AC_t[10], AC_t[11]}), .TTY_OUT(TTY_OUT),
    .TTY_enable(TTY_enable));

  assign {STATE[31:28], STATE[7:6], STATE[4]} = {7{1'b0}};

  // Other names for the same wires on the sheet: AND = OPCODE[0]; B[2:0] = STATE[23:21]; CIN = STATE[24];
  //   CLRP_H = STATE[26]; CONTP_H = STATE[27]; CP_MUX[2:0] = {STATE[13], STATE[14], STATE[15]}; DCA = OPCODE[3];
  //   DEFER = STATE[2]; DEP = DEPOSIT; EXEC = STATE[1]; FETCH = STATE[0]; FETCH1 = STATE[11]; FETCH2 = STATE[10];
  //   FETCH4 = STATE[9]; FETCH8 = STATE[8]; IE = STATE[3]; IOT = OPCODE[6]; ISZ = OPCODE[2]; JMP = OPCODE[5];
  //   JMS = OPCODE[4]; LDAC = LD_AC; LDIR = LD_IR; LDM = LD_MEM; LDMA = LD_MA; LDMB = LD_MB; LDPC = LD_PC;
  //   MANSW = STATE[25]; MIC = OPCODE[7]; MODE = STATE[20]; RUN = STATE[5];
  //   S[3:0] = {STATE[16], STATE[17], STATE[18], STATE[19]}; TAD = OPCODE[1]; WRITE = STATE[12]

  // Notes on the sheet:
  //   Clock: Hz: 2147483647
  //   CLK_Mode: default 1
  //   CLR: default 1
  //   LD_PC: default 1
  //   LD_IR: default 1
  //   LD_MB: default 1
  //   LD_MEM: default 1
  //   LD_MA: default 1
  //   LD_AC: default 1
  //   DEPOSIT: default 1
  //   EXAMINE: default 1
  //   CONT: default 1
  //   STOP: default 1
  //   SINGINST: default 1
  //   nCLRIN: default 1
  //   ALU
  //   S M ~C Function
  //     0 0 0 PASS
  //     0 0 1 INCREMENT
  //     0 1 0 NOT
  //     1 0 0 OR
  //     3 1 0 ZERO
  //     9 0 0 PLUS
  //   12 0 1 AND
  //   AC
  //   M
  //   IR
  //   PC
  //   MB
  //   MA
  //   MUX
  //   00: PC
  //   01: MB
  //   02: MA
  //   03: AC
  //   04: IORD
  //   05: SR
  //   06: M
  //   07: EA
endmodule
