// Digital circuit Panel.dig as structural Verilog
module Panel (
  input  clk,
  input  Manual_Auto,
  input  SingleInstuction,
  input  in_4,
  input  in_5,
  input  in_6,
  input  in_7,
  input  in_8,
  input  in_9,
  input  in_10,
  input  in_11,
  input  in_12,
  input  in_13,
  input  in_14,
  input  in_15
);

  wire B_0, B_2, B_4, CIN, CLK_out, CLR_out, CLR_TTY_out, CLRP_H, CONT_out, CONTP_H, CP_0, CP_2, CP_4,
       decoder_1_out_0, decoder_1_out_1, decoder_1_out_2, decoder_1_out_3, decoder_1_out_4, decoder_1_out_5,
       decoder_1_out_6, decoder_1_out_7, decoder_2_out_0, decoder_2_out_1, decoder_2_out_2, decoder_2_out_3,
       decoder_2_out_4, decoder_2_out_5, decoder_2_out_6, decoder_2_out_7, DEFER, DEPOSIT_out, EXAMINE_out,
       EXEC, FETCH, FETCH1, FETCH2, FETCH4, FETCH8, IE, keyboard_1_av, LD_AC_out, LD_IR_out, LD_MA_out,
       LD_MB_out, LD_MEM_out, LD_PC_out, LINK, MANSW, MODE, pdp_8_1_tty_enable, pdp_8_1_tty_out_print, RUN,
       S_0, S_1, S_2, S_3, STOP_out, TTY_IN_CLOCK, WRITE;
  wire [7:0] not_1_out, pdp_8_1_opcode, pdp_8_1_tty_out;
  wire [11:0] pdp_8_1_ac, pdp_8_1_ir, pdp_8_1_ma, pdp_8_1_mb, pdp_8_1_mem, pdp_8_1_pc;
  wire [15:0] keyboard_1_d;
  wire [31:4] pdp_8_1_state;

  Button u_CLK (.out(CLK_out));
  Button #(.activeLow("true")) CLR (.out(CLR_out));
  Button #(.activeLow("true")) LD_PC (.out(LD_PC_out));
  Button #(.activeLow("true")) LD_IR (.out(LD_IR_out));
  Button #(.activeLow("true")) LD_MB (.out(LD_MB_out));
  Button #(.activeLow("true")) LD_MEM (.out(LD_MEM_out));
  Button #(.activeLow("true")) LD_MA (.out(LD_MA_out));
  Button #(.activeLow("true")) LD_AC (.out(LD_AC_out));
  Button #(.activeLow("true")) DEPOSIT (.out(DEPOSIT_out));
  Button #(.activeLow("true")) EXAMINE (.out(EXAMINE_out));
  Button #(.activeLow("true")) CONT (.out(CONT_out));
  Button #(.activeLow("true")) STOP (.out(STOP_out));
  Button #(.activeLow("true")) CLR_TTY (.out(CLR_TTY_out));
  Keyboard keyboard_1 (.C(TTY_IN_CLOCK), .en(1'b1), .D(keyboard_1_d), .av(keyboard_1_av));
  Decoder #(.Selector_Bits(3)) decoder_1 (
    .sel({B_4, B_2, B_0}), .out_0(decoder_1_out_0), .out_1(decoder_1_out_1), .out_2(decoder_1_out_2),
    .out_3(decoder_1_out_3), .out_4(decoder_1_out_4), .out_5(decoder_1_out_5), .out_6(decoder_1_out_6),
    .out_7(decoder_1_out_7));
  PDP_8 pdp_8_1 (
    .Clock(clk), .CLK_Mode(Manual_Auto), .Manual_Clock(CLK_out), .KBD_IN(keyboard_1_d),
    .KBD_CLK(keyboard_1_av), .CLR(CLR_out), .LD_PC(LD_PC_out), .LD_IR(LD_IR_out), .LD_MB(LD_MB_out),
    .LD_MEM(LD_MEM_out), .LD_MA(LD_MA_out), .LD_AC(LD_AC_out), .DEPOSIT(DEPOSIT_out), .EXAMINE(EXAMINE_out),
    .CONT(CONT_out), .STOP(STOP_out), .SINGINST(SingleInstuction), .nCLRIN(CLR_TTY_out),
    .SR({in_15, in_14, in_13, in_12, in_11, in_10, in_9, in_8, in_7, in_6, in_5, in_4}),
    .TTY_OUT(pdp_8_1_tty_out), .TTY_OUT_PRINT(pdp_8_1_tty_out_print), .TTY_enable(pdp_8_1_tty_enable),
    .TTY_IN_CLK(TTY_IN_CLOCK), .OPCODE(pdp_8_1_opcode), .PC(pdp_8_1_pc), .MB(pdp_8_1_mb), .MA(pdp_8_1_ma),
    .AC(pdp_8_1_ac), .MEM(pdp_8_1_mem), .IR(pdp_8_1_ir),
    .STATE({pdp_8_1_state[31:28], CONTP_H, CLRP_H, MANSW, CIN, B_4, B_2, B_0, MODE, S_0, S_1, S_2, S_3, CP_0, CP_2, CP_4, WRITE, FETCH1, FETCH2, FETCH4, FETCH8, pdp_8_1_state[7:6], RUN, pdp_8_1_state[4], IE, DEFER, EXEC, FETCH}),
    .LINK(LINK));
  // Probe on {FETCH8, FETCH4, FETCH2, FETCH1}
  // Probe on {B_4, B_2, B_0}
  LED PC (.in(decoder_1_out_0));
  LED MB (.in(decoder_1_out_1));
  LED MA (.in(decoder_1_out_2));
  LED AC (.in(decoder_1_out_3));
  LED IORD (.in(decoder_1_out_4));
  LED SR (.in(decoder_1_out_5));
  LED Mem (.in(decoder_1_out_6));
  LED EA (.in(decoder_1_out_7));
  // Probe on {CP_4, CP_2, CP_0}
  Decoder #(.Selector_Bits(3)) decoder_2 (
    .sel({CP_4, CP_2, CP_0}), .out_0(decoder_2_out_0), .out_1(decoder_2_out_1), .out_2(decoder_2_out_2),
    .out_3(decoder_2_out_3), .out_4(decoder_2_out_4), .out_5(decoder_2_out_5), .out_6(decoder_2_out_6),
    .out_7(decoder_2_out_7));
  // Probe on {S_3, S_2, S_1, S_0}
  // Probe on MODE
  // Probe on CIN
  LED CP0 (.in(decoder_2_out_0));
  LED CP1 (.in(decoder_2_out_1));
  LED CP2 (.in(decoder_2_out_2));
  LED CP3 (.in(decoder_2_out_3));
  LED CP4 (.in(decoder_2_out_4));
  LED CP5 (.in(decoder_2_out_5));
  LED CP6 (.in(decoder_2_out_6));
  LED CP7 (.in(decoder_2_out_7));
  Terminal #(.termWidth(80), .termHeight(24)) terminal_1 (
    .D(pdp_8_1_tty_out), .C(pdp_8_1_tty_out_print), .en(pdp_8_1_tty_enable));
  LED led_1 (.in(LINK));
  LED led_2 (.in(pdp_8_1_pc[11]));
  LED led_3 (.in(pdp_8_1_pc[10]));
  LED led_4 (.in(pdp_8_1_mb[11]));
  LED led_5 (.in(pdp_8_1_mb[10]));
  LED led_6 (.in(pdp_8_1_ma[11]));
  LED led_7 (.in(pdp_8_1_ma[10]));
  LED led_8 (.in(pdp_8_1_ac[11]));
  LED led_9 (.in(pdp_8_1_ac[10]));
  LED led_10 (.in(pdp_8_1_mem[11]));
  LED led_11 (.in(pdp_8_1_mem[10]));
  LED led_12 (.in(pdp_8_1_ir[11]));
  LED led_13 (.in(pdp_8_1_ir[10]));
  LED led_14 (.in(in_15));
  LED led_15 (.in(in_14));
  LED led_16 (.in(pdp_8_1_pc[9]));
  LED led_17 (.in(pdp_8_1_pc[8]));
  LED led_18 (.in(pdp_8_1_mb[9]));
  LED led_19 (.in(pdp_8_1_mb[8]));
  LED led_20 (.in(pdp_8_1_ma[9]));
  LED led_21 (.in(pdp_8_1_ma[8]));
  LED led_22 (.in(pdp_8_1_ac[9]));
  LED led_23 (.in(pdp_8_1_ac[8]));
  LED led_24 (.in(pdp_8_1_mem[9]));
  LED led_25 (.in(pdp_8_1_mem[8]));
  LED led_26 (.in(pdp_8_1_ir[8]));
  LED led_27 (.in(pdp_8_1_ir[9]));
  LED led_28 (.in(in_13));
  LED led_29 (.in(in_12));
  LED led_30 (.in(pdp_8_1_pc[7]));
  LED led_31 (.in(pdp_8_1_pc[6]));
  LED led_32 (.in(pdp_8_1_mb[7]));
  LED led_33 (.in(pdp_8_1_mb[6]));
  LED led_34 (.in(pdp_8_1_ma[7]));
  LED led_35 (.in(pdp_8_1_ma[6]));
  LED led_36 (.in(pdp_8_1_ac[7]));
  LED led_37 (.in(pdp_8_1_ac[6]));
  LED led_38 (.in(pdp_8_1_mem[7]));
  LED led_39 (.in(pdp_8_1_mem[6]));
  LED led_40 (.in(pdp_8_1_ir[7]));
  LED led_41 (.in(pdp_8_1_ir[6]));
  LED led_42 (.in(in_11));
  LED led_43 (.in(in_10));
  LED led_44 (.in(pdp_8_1_pc[5]));
  LED led_45 (.in(pdp_8_1_pc[4]));
  LED led_46 (.in(pdp_8_1_mb[5]));
  LED led_47 (.in(pdp_8_1_mb[4]));
  LED led_48 (.in(pdp_8_1_ma[5]));
  LED led_49 (.in(pdp_8_1_ma[4]));
  LED led_50 (.in(pdp_8_1_ac[5]));
  LED led_51 (.in(pdp_8_1_ac[4]));
  LED led_52 (.in(pdp_8_1_mem[5]));
  LED led_53 (.in(pdp_8_1_mem[4]));
  LED led_54 (.in(pdp_8_1_ir[5]));
  LED led_55 (.in(pdp_8_1_ir[4]));
  LED led_56 (.in(in_9));
  LED led_57 (.in(in_8));
  LED led_58 (.in(pdp_8_1_pc[3]));
  LED led_59 (.in(pdp_8_1_pc[2]));
  LED led_60 (.in(pdp_8_1_mb[3]));
  LED led_61 (.in(pdp_8_1_mb[2]));
  LED led_62 (.in(pdp_8_1_ma[3]));
  LED led_63 (.in(pdp_8_1_ma[2]));
  LED led_64 (.in(pdp_8_1_ac[3]));
  LED led_65 (.in(pdp_8_1_ac[2]));
  LED led_66 (.in(pdp_8_1_mem[3]));
  LED led_67 (.in(pdp_8_1_mem[2]));
  LED led_68 (.in(pdp_8_1_ir[3]));
  LED led_69 (.in(pdp_8_1_ir[2]));
  LED led_70 (.in(in_7));
  LED led_71 (.in(in_6));
  LED led_72 (.in(pdp_8_1_pc[1]));
  LED led_73 (.in(pdp_8_1_pc[0]));
  LED led_74 (.in(pdp_8_1_mb[1]));
  LED led_75 (.in(pdp_8_1_mb[0]));
  LED led_76 (.in(pdp_8_1_ma[1]));
  LED led_77 (.in(pdp_8_1_ma[0]));
  LED led_78 (.in(pdp_8_1_ac[1]));
  LED led_79 (.in(pdp_8_1_ac[0]));
  LED led_80 (.in(pdp_8_1_mem[1]));
  LED led_81 (.in(pdp_8_1_mem[0]));
  LED led_82 (.in(pdp_8_1_ir[1]));
  LED led_83 (.in(pdp_8_1_ir[0]));
  LED led_84 (.in(in_5));
  LED led_85 (.in(in_4));
  assign not_1_out = ~pdp_8_1_opcode;  // Not not_1, 8 bits wide
  // Probe on pdp_8_1_pc
  // Probe on pdp_8_1_mb
  // Probe on pdp_8_1_ma
  // Probe on pdp_8_1_ac
  // Probe on pdp_8_1_mem
  // Probe on pdp_8_1_ir
  LED AND (.in(not_1_out[0]));
  LED TAD (.in(not_1_out[1]));
  LED ISZ (.in(not_1_out[2]));
  LED DCA (.in(not_1_out[3]));
  LED JMS (.in(not_1_out[4]));
  LED JMP (.in(not_1_out[5]));
  LED IOT (.in(not_1_out[6]));
  LED OPR (.in(not_1_out[7]));
  LED u_FETCH (.in(FETCH));
  LED EXECUTE (.in(EXEC));
  LED u_DEFER (.in(DEFER));
  LED u_IE (.in(IE));
  LED u_RUN (.in(RUN));

  // Notes on the sheet:
  //   clk: Hz: 2147483647
  //   SingleInstuction: default 1
  //   Fetch-State
  //   Datapath-MUX
  //   ALU-Func.
  //   Control Pulses
  //   4
  //   3
  //   2
  //   1
  //   PC
  //   MB
  //   MA
  //   AC
  //   MEM
  //   IR
  //   SR
endmodule
