// Digital circuit TTY-Logic.dig as structural Verilog
module TTY_Logic (
  input  [11:0] IR,
  input  nCLRIN,
  input  IOP1_H,
  input  IOP2_H,
  input  IOP4_H,
  input  IOP1_L,
  input  TTY_IN_DATA_AVAILABLE,
  input  [15:0] KBDIN,
  output PINT_PRINTER,
  output TTY_IN_CLOCK,
  output TTY_OUT_PRINT,
  output IOS_PRINTER,
  output PINT_KEYBOARD,
  output IOS_KEYBOARD,
  output RDA,
  output RDE,
  output [11:0] KBDOUT
);

  wire and_1_out, and_2_out, and_4_out, and_5_out, and_6_out, and_7_out, d_ff_as_1_q, lt_LF_gt___eq__0x0A_eq,
       nor_1_out, not_1_out, not_4_out, not_5_out, or_1_out, or_2_out, or_3_out, TTY_IN, TTY_OUT;
  wire [7:0] Data_Latch_q, multiplexer_1_out;

  and and_1 (and_1_out, IOP4_H, TTY_IN);
  not not_1 (not_1_out, nCLRIN);
  and and_2 (and_2_out, IOP4_H, TTY_IN);
  not not_2 (RDA, and_1_out);
  or or_1 (or_1_out, and_1_out, not_1_out);
  and and_3 (TTY_IN_CLOCK, TTY_IN_DATA_AVAILABLE, and_2_out);
  D_FF #(.Bits(8)) Data_Latch (.D(KBDIN[7:0]), .C(TTY_IN_DATA_AVAILABLE), .Q(Data_Latch_q));  // open: nQ
  D_FF_AS d_ff_as_1 (.Set(1'b0), .D(1'b1), .C(TTY_IN_DATA_AVAILABLE), .Clr(or_1_out), .Q(d_ff_as_1_q));  // open: nQ
  Comparator #(.Bits(8)) lt_LF_gt___eq__0x0A (.a(Data_Latch_q), .b(8'ha), .eq(lt_LF_gt___eq__0x0A_eq));  // open: gt, lt
  Comparator #(.Bits(6)) x03x (.a(IR[8:3]), .b(6'b110000), .eq(TTY_IN));  // open: gt, lt
  Comparator #(.Bits(6)) x04x (.a(IR[8:3]), .b(6'b001000), .eq(TTY_OUT));  // open: gt, lt
  or or_2 (or_2_out, IOP1_H, IOP2_H, IOP4_H);
  nor nor_1 (nor_1_out, IOP1_L, IR[10]);
  Multiplexer #(.Bits(8)) multiplexer_1 (
    .sel(lt_LF_gt___eq__0x0A_eq), .in_0(Data_Latch_q), .in_1(8'hd), .out(multiplexer_1_out));
  nand nand_1 (IOS_KEYBOARD, d_ff_as_1_q, nor_1_out, TTY_IN);
  and and_4 (and_4_out, or_2_out, TTY_IN);
  not not_3 (PINT_KEYBOARD, d_ff_as_1_q);
  and and_5 (and_5_out, IOP4_H, TTY_OUT);
  and and_6 (and_6_out, IOP2_H, TTY_OUT);
  assign KBDOUT = and_4_out ? {multiplexer_1_out[0], multiplexer_1_out[1], multiplexer_1_out[2], multiplexer_1_out[3], multiplexer_1_out[4], multiplexer_1_out[5], multiplexer_1_out[6], 5'b10000} : 12'bz;  // Driver driver_1
  Driver #(.invertDriverOutput("true")) driver_2 (.in(and_2_out), .en(and_2_out));  // open: out
  not not_4 (not_4_out, nCLRIN);
  and and_7 (and_7_out, and_5_out, not_5_out);
  not not_5 (not_5_out, or_3_out);
  or or_3 (or_3_out, and_6_out, not_4_out);
  D_FF_AS d_ff_as_2 (.Set(and_7_out), .D(1'b1), .C(1'b0), .Clr(or_3_out), .Q(TTY_OUT_PRINT));  // open: nQ
  not not_6 (PINT_PRINTER, TTY_OUT_PRINT);
  nand nand_2 (IOS_PRINTER, TTY_OUT_PRINT, IOP1_H, TTY_OUT);

  // Notes on the sheet:
  //   <CR> = 0x0D
  //   IF IOP & TTY.IN drive
  //   KBDOUT to INPUT-BUS.
endmodule
