// Digital circuit TTYMOD.dig as structural Verilog
module TTYMOD (
  input  [7:0] TTY_IN,
  output [7:0] TTY_OUT,
  output TTY_enable
);

  wire comparator_1_gt, comparator_1_lt;

  Comparator #(.Bits(8)) comparator_1 (.a(8'ha), .b(TTY_IN), .gt(comparator_1_gt), .lt(comparator_1_lt));  // open: eq
  or or_1 (TTY_enable, comparator_1_gt, comparator_1_lt);

  assign TTY_OUT = TTY_IN;
endmodule
